// Logisim project ALU.circ as structural Verilog: 1 circuit, main circuit main
module main (
  input  CS0,
  input  CS2,
  input  CS1,
  input  A1,
  input  B1,
  input  A2,
  input  B2,
  input  A3,
  input  B3,
  input  A4,
  input  B4,
  output F1,
  output F2,
  output F3,
  output F4,
  output C,
  output V,
  output Z,
  output S
);

  wire adder_1_cout, adder_2_cout, adder_3_cout, adder_4_cout, and_1_out, and_2_out, and_3_out, and_4_out,
       and_5_out, and_6_out, and_7_out, and_8_out, and_9_out, and_11_out, and_12_out, and_13_out, and_14_out,
       not_1_out, not_2_out, not_3_out, or_1_out, or_2_out, or_3_out, or_4_out, or_5_out, or_6_out, or_7_out,
       xor_1_out;

  not not_1 (not_1_out, CS1);
  and and_1 (and_1_out, CS2, not_1_out);
  xor xor_1 (xor_1_out, CS1, CS2);
  not not_2 (not_2_out, xor_1_out);
  and and_2 (and_2_out, and_1_out, B1);
  and and_3 (and_3_out, and_1_out, B2);
  and and_4 (and_4_out, and_1_out, B3);
  and and_5 (and_5_out, and_1_out, B4);
  or or_1 (or_1_out, A1, and_2_out);
  and and_6 (and_6_out, B1, not_2_out);
  or or_2 (or_2_out, A2, and_3_out);
  and and_7 (and_7_out, B2, not_2_out);
  or or_3 (or_3_out, A3, and_4_out);
  and and_8 (and_8_out, B3, not_2_out);
  or or_4 (or_4_out, A4, and_5_out);
  and and_9 (and_9_out, B4, not_2_out);
  not not_3 (not_3_out, CS2);
  and and_10 (C, not_3_out, adder_4_cout);
  and and_11 (and_11_out, not_3_out, CS0);
  Adder #(.width(1)) adder_1 (.a(or_1_out), .b(and_6_out), .out(F1), .cin(and_11_out), .cout(adder_1_cout));
  and and_12 (and_12_out, not_3_out, adder_1_cout);
  Adder #(.width(1)) adder_2 (.a(or_2_out), .b(and_7_out), .out(F2), .cin(and_12_out), .cout(adder_2_cout));
  and and_13 (and_13_out, not_3_out, adder_2_cout);
  Adder #(.width(1)) adder_3 (.a(or_3_out), .b(and_8_out), .out(F3), .cin(and_13_out), .cout(adder_3_cout));
  and and_14 (and_14_out, not_3_out, adder_3_cout);
  Adder #(.width(1)) adder_4 (.a(or_4_out), .b(and_9_out), .out(F4), .cin(and_14_out), .cout(adder_4_cout));
  xor xor_2 (V, C, and_14_out);
  or or_5 (or_5_out, F1, F2);
  or or_6 (or_6_out, or_5_out, or_7_out);
  not not_4 (Z, or_6_out);
  or or_7 (or_7_out, F3, F4);

  assign S = F4;
endmodule
